// Logisim project CPU.circ as structural Verilog: 5 circuits, main circuit implementation
module implementation (
  input  [15:0] Instruction_In,
  input  ClkIn,
  output [4:0] Instruction_Address_Out,
  output [3:0] Reg0_Out,
  output [3:0] Reg1_Out,
  output [3:0] Reg2_Out,
  output [3:0] Reg3_Out,
  output [3:0] Reg4_Out,
  output [3:0] Reg5_Out,
  output [3:0] Reg6_Out,
  output [3:0] Reg7_Out,
  output [3:0] Reg8_Out,
  output [3:0] Reg9_Out,
  output [3:0] Reg10_Out,
  output [3:0] Reg11_Out,
  output [3:0] Reg12_Out,
  output [3:0] Reg13_Out,
  output [3:0] Reg14_Out,
  output [3:0] Reg15_Out
);

  wire IsImmediatee, LOAD, MOVE, not_1_out, RegWrite, STOP, StopCPU, STOPTrue, xor_1_out;
  wire [2:0] ALU_OPCHOICE;
  wire [3:0] A_Value, ALU_Result, B_Value, multiplexer_2_out, multiplexer_3_out, multiplexer_4_out;
  wire [4:0] adder_1_out, multiplexer_1_out;

  Adder #(.width(5)) adder_1 (.a(5'b00001), .b(Instruction_Address_Out), .out(adder_1_out));  // open: cin, cout
  Register #(.width(1)) register_1 (.D(STOPTrue), .en(not_1_out), .clk(ClkIn), .Q(StopCPU));  // open: clr
  not not_1 (not_1_out, STOP);
  // Probe on StopCPU
  xor xor_1 (xor_1_out, StopCPU, 1'b1);
  // Probe on multiplexer_1_out
  Multiplexer #(.enable("false"), .width(5)) multiplexer_1 (
    .in0(adder_1_out), .in1(Instruction_Address_Out), .out(multiplexer_1_out), .sel(STOPTrue));
  Register #(.width(5)) register_2 (
    .D(multiplexer_1_out), .en(xor_1_out), .clk(ClkIn), .Q(Instruction_Address_Out));  // open: clr
  // Probe on Instruction_Address_Out
  Multiplexer #(.enable("false"), .width(4)) multiplexer_2 (
    .in0(ALU_Result), .in1(Instruction_In[3:0]), .out(multiplexer_2_out), .sel(LOAD));
  ControlPath controlpath_1 (
    .OpCode(Instruction_In[15:12]), .IsWrite(RegWrite), .LOADOUT(LOAD), .MOVE(MOVE),
    .IsImmediateOut(IsImmediatee), .ALU_OP_CHOICE_OUT(ALU_OPCHOICE), .Stop(STOP), .StopTrue(STOPTrue));
  Multiplexer #(.enable("false"), .width(4)) multiplexer_3 (
    .in0(multiplexer_2_out), .in1(A_Value), .out(multiplexer_3_out), .sel(MOVE));
  RegFile regfile_1 (
    .A_Sel_In(Instruction_In[7:4]), .B_Sel_In(Instruction_In[3:0]), .C_Sel_In(Instruction_In[11:8]),
    .Data_In(multiplexer_3_out), .Reg_Write_In(RegWrite), .clk_in(ClkIn), .A_Out(A_Value), .B_Out(B_Value),
    .Reg0_Out(Reg0_Out), .Reg1_Out(Reg1_Out), .Reg2_Out(Reg2_Out), .Reg3_Out(Reg3_Out), .Reg4_Out(Reg4_Out),
    .Reg5_Out(Reg5_Out), .Reg6_Out(Reg6_Out), .Reg7_Out(Reg7_Out), .Reg8_Out(Reg8_Out), .Reg9_Out(Reg9_Out),
    .Reg10_Out(Reg10_Out), .Reg11_Out(Reg11_Out), .Reg12_Out(Reg12_Out), .Reg13_Out(Reg13_Out),
    .Reg14_Out(Reg14_Out), .Reg15_Out(Reg15_Out));
  Multiplexer #(.enable("false"), .width(4)) multiplexer_4 (
    .in0(B_Value), .in1(Instruction_In[3:0]), .out(multiplexer_4_out), .sel(IsImmediatee));
  ALU alu_1 (.ALU_OP_IN(ALU_OPCHOICE), .A_in(A_Value), .B_in(multiplexer_4_out), .ALU_Result(ALU_Result));

  // Other names for the same wires on the sheet: Clk = ClkIn; Immediate[3:0] = Instruction_In[3:0];
  //   Instruction[15:0] = Instruction_In; RB[3:0] = Instruction_In[3:0]; RA[3:0] = Instruction_In[7:4];
  //   RC[3:0] = Instruction_In[11:8]; Opcode[3:0] = Instruction_In[15:12];
  //   Instruction_Address[4:0] = Instruction_Address_Out; Reg0[3:0] = Reg0_Out; Reg1[3:0] = Reg1_Out;
  //   Reg2[3:0] = Reg2_Out; Reg3[3:0] = Reg3_Out; Reg4[3:0] = Reg4_Out; Reg5[3:0] = Reg5_Out; Reg6[3:0] = Reg6_Out;
  //   Reg7[3:0] = Reg7_Out; Reg8[3:0] = Reg8_Out; Reg9[3:0] = Reg9_Out; Reg10[3:0] = Reg10_Out;
  //   Reg11[3:0] = Reg11_Out; Reg12[3:0] = Reg12_Out; Reg13[3:0] = Reg13_Out; Reg14[3:0] = Reg14_Out;
  //   Reg15[3:0] = Reg15_Out

  // Notes on the sheet:
  //   PC counter, R type, I type 
endmodule

module RegFile (
  input  [3:0] A_Sel_In,
  input  [3:0] B_Sel_In,
  input  [3:0] C_Sel_In,
  input  [3:0] Data_In,
  input  Reg_Write_In,
  input  clk_in,
  output [3:0] A_Out,
  output [3:0] B_Out,
  output [3:0] Reg0_Out,
  output [3:0] Reg1_Out,
  output [3:0] Reg2_Out,
  output [3:0] Reg3_Out,
  output [3:0] Reg4_Out,
  output [3:0] Reg5_Out,
  output [3:0] Reg6_Out,
  output [3:0] Reg7_Out,
  output [3:0] Reg8_Out,
  output [3:0] Reg9_Out,
  output [3:0] Reg10_Out,
  output [3:0] Reg11_Out,
  output [3:0] Reg12_Out,
  output [3:0] Reg13_Out,
  output [3:0] Reg14_Out,
  output [3:0] Reg15_Out
);

  wire Reg_Write0, Reg_Write1, Reg_Write2, Reg_Write3, Reg_Write4, Reg_Write5, Reg_Write6, Reg_Write7,
       Reg_Write8, Reg_Write9, Reg_Write10, Reg_Write11, Reg_Write12, Reg_Write13, Reg_Write14, Reg_Write15;

  Demultiplexer #(.enable("false"), .select(4)) demultiplexer_1 (
    .out0(Reg_Write0), .out1(Reg_Write1), .out2(Reg_Write2), .out3(Reg_Write3), .out4(Reg_Write4),
    .out5(Reg_Write5), .out6(Reg_Write6), .out7(Reg_Write7), .out8(Reg_Write8), .out9(Reg_Write9),
    .out10(Reg_Write10), .out11(Reg_Write11), .out12(Reg_Write12), .out13(Reg_Write13), .out14(Reg_Write14),
    .out15(Reg_Write15), .in(Reg_Write_In), .sel(C_Sel_In));
  Register #(.width(4)) register_1 (.D(Data_In), .en(Reg_Write0), .clk(clk_in), .Q(Reg0_Out));  // open: clr
  Register #(.width(4)) register_2 (.D(Data_In), .en(Reg_Write4), .clk(clk_in), .Q(Reg4_Out));  // open: clr
  Register #(.width(4)) register_3 (.D(Data_In), .en(Reg_Write8), .clk(clk_in), .Q(Reg8_Out));  // open: clr
  Register #(.width(4)) register_4 (.D(Data_In), .en(Reg_Write12), .clk(clk_in), .Q(Reg12_Out));  // open: clr
  Register #(.width(4)) register_5 (.D(Data_In), .en(Reg_Write1), .clk(clk_in), .Q(Reg1_Out));  // open: clr
  Register #(.width(4)) register_6 (.D(Data_In), .en(Reg_Write5), .clk(clk_in), .Q(Reg5_Out));  // open: clr
  Register #(.width(4)) register_7 (.D(Data_In), .en(Reg_Write9), .clk(clk_in), .Q(Reg9_Out));  // open: clr
  Register #(.width(4)) register_8 (.D(Data_In), .en(Reg_Write13), .clk(clk_in), .Q(Reg13_Out));  // open: clr
  Register #(.width(4)) register_9 (.D(Data_In), .en(Reg_Write2), .clk(clk_in), .Q(Reg2_Out));  // open: clr
  Register #(.width(4)) register_10 (.D(Data_In), .en(Reg_Write6), .clk(clk_in), .Q(Reg6_Out));  // open: clr
  Register #(.width(4)) register_11 (.D(Data_In), .en(Reg_Write10), .clk(clk_in), .Q(Reg10_Out));  // open: clr
  Register #(.width(4)) register_12 (.D(Data_In), .en(Reg_Write14), .clk(clk_in), .Q(Reg14_Out));  // open: clr
  Register #(.width(4)) register_13 (.D(Data_In), .en(Reg_Write3), .clk(clk_in), .Q(Reg3_Out));  // open: clr
  Register #(.width(4)) register_14 (.D(Data_In), .en(Reg_Write7), .clk(clk_in), .Q(Reg7_Out));  // open: clr
  Register #(.width(4)) register_15 (.D(Data_In), .en(Reg_Write11), .clk(clk_in), .Q(Reg11_Out));  // open: clr
  Register #(.width(4)) register_16 (.D(Data_In), .en(Reg_Write15), .clk(clk_in), .Q(Reg15_Out));  // open: clr
  Multiplexer #(.enable("false"), .select(4), .width(4)) multiplexer_1 (
    .in0(Reg0_Out), .in1(Reg1_Out), .in2(Reg2_Out), .in3(Reg3_Out), .in4(Reg4_Out), .in5(Reg5_Out),
    .in6(Reg6_Out), .in7(Reg7_Out), .in8(Reg8_Out), .in9(Reg9_Out), .in10(Reg10_Out), .in11(Reg11_Out),
    .in12(Reg12_Out), .in13(Reg13_Out), .in14(Reg14_Out), .in15(Reg15_Out), .out(A_Out), .sel(A_Sel_In));
  Multiplexer #(.enable("false"), .select(4), .width(4)) multiplexer_2 (
    .in0(Reg0_Out), .in1(Reg1_Out), .in2(Reg2_Out), .in3(Reg3_Out), .in4(Reg4_Out), .in5(Reg5_Out),
    .in6(Reg6_Out), .in7(Reg7_Out), .in8(Reg8_Out), .in9(Reg9_Out), .in10(Reg10_Out), .in11(Reg11_Out),
    .in12(Reg12_Out), .in13(Reg13_Out), .in14(Reg14_Out), .in15(Reg15_Out), .out(B_Out), .sel(B_Sel_In));

  // Other names for the same wires on the sheet: A[3:0] = A_Out; A_Sel[3:0] = A_Sel_In; B[3:0] = B_Out;
  //   B_Sel[3:0] = B_Sel_In; C_Sel[3:0] = C_Sel_In; clk = clk_in; Data[3:0] = Data_In; Reg0[3:0] = Reg0_Out;
  //   Reg1[3:0] = Reg1_Out; Reg2[3:0] = Reg2_Out; Reg3[3:0] = Reg3_Out; Reg4[3:0] = Reg4_Out; Reg5[3:0] = Reg5_Out;
  //   Reg6[3:0] = Reg6_Out; Reg7[3:0] = Reg7_Out; Reg8[3:0] = Reg8_Out; Reg9[3:0] = Reg9_Out; Reg10[3:0] = Reg10_Out;
  //   Reg11[3:0] = Reg11_Out; Reg12[3:0] = Reg12_Out; Reg13[3:0] = Reg13_Out; Reg14[3:0] = Reg14_Out;
  //   Reg15[3:0] = Reg15_Out; Reg_Write = Reg_Write_In
endmodule

module ALU (
  input  [2:0] ALU_OP_IN,
  input  [3:0] A_in,
  input  [3:0] B_in,
  output [3:0] ALU_Result
);

  wire [3:0] adder_1_out, and_1_out, negator_1_out, not_1_out, or_1_out, subtractor_1_out, xor_1_out;

  assign and_1_out = A_in & B_in;  // AND_Gate and_1, 4 bits wide
  assign or_1_out = A_in | B_in;  // OR_Gate or_1, 4 bits wide
  assign xor_1_out = A_in ^ B_in;  // XOR_Gate xor_1, 4 bits wide
  assign not_1_out = ~A_in;  // NOT_Gate not_1, 4 bits wide
  Negator #(.width(4)) negator_1 (.in(A_in), .out(negator_1_out));
  Adder #(.width(4)) adder_1 (.a(A_in), .b(B_in), .out(adder_1_out));  // open: cin, cout
  Subtractor #(.width(4)) subtractor_1 (.a(A_in), .b(B_in), .out(subtractor_1_out));  // open: bin, bout
  Multiplexer #(.enable("false"), .select(3), .width(4)) multiplexer_1 (
    .in0(and_1_out), .in1(or_1_out), .in2(xor_1_out), .in3(not_1_out), .in4(negator_1_out),
    .in5(adder_1_out), .in6(subtractor_1_out), .out(ALU_Result), .sel(ALU_OP_IN));  // open: in7

  // Other names for the same wires on the sheet: A[3:0] = A_in; ALU_OP[2:0] = ALU_OP_IN; B[3:0] = B_in
endmodule

module ControlPath (
  input  [3:0] OpCode,
  output IsWrite,
  output LOADOUT,
  output MOVE,
  output IsImmediateOut,
  output [2:0] ALU_OP_CHOICE_OUT,
  output Stop,
  output StopTrue
);

  wire ADDI, ADDR, ANDI, ANDR, NEGATE, NOP, NOTInst, or_1_out, or_2_out, or_3_out, or_4_out, or_5_out,
       or_6_out, ORI, ORR, SUBI, SUBR, XORI, XORR;

  Comparator #(.width(4)) comparator_1 (.a(OpCode), .b(4'b0000), .eq(StopTrue));  // open: gt, lt
  Comparator #(.width(4)) comparator_2 (.a(OpCode), .b(4'b0001), .eq(NOP));  // open: gt, lt
  Comparator #(.width(4)) comparator_3 (.a(OpCode), .b(4'b0010), .eq(LOADOUT));  // open: gt, lt
  Comparator #(.width(4)) comparator_4 (.a(OpCode), .b(4'b0011), .eq(MOVE));  // open: gt, lt
  Comparator #(.width(4)) comparator_5 (.a(OpCode), .b(4'b0100), .eq(ANDR));  // open: gt, lt
  Comparator #(.width(4)) comparator_6 (.a(OpCode), .b(4'b0101), .eq(ANDI));  // open: gt, lt
  Comparator #(.width(4)) comparator_7 (.a(OpCode), .b(4'b0110), .eq(ORR));  // open: gt, lt
  Comparator #(.width(4)) comparator_8 (.a(OpCode), .b(4'b0111), .eq(ORI));  // open: gt, lt
  Comparator #(.width(4)) comparator_9 (.a(OpCode), .b(4'b1000), .eq(XORR));  // open: gt, lt
  Comparator #(.width(4)) comparator_10 (.a(OpCode), .b(4'b1001), .eq(XORI));  // open: gt, lt
  Comparator #(.width(4)) comparator_11 (.a(OpCode), .b(4'b1010), .eq(NOTInst));  // open: gt, lt
  Comparator #(.width(4)) comparator_12 (.a(OpCode), .b(4'b1011), .eq(NEGATE));  // open: gt, lt
  Comparator #(.width(4)) comparator_13 (.a(OpCode), .b(4'b1100), .eq(ADDR));  // open: gt, lt
  Comparator #(.width(4)) comparator_14 (.a(OpCode), .b(4'b1101), .eq(ADDI));  // open: gt, lt
  Comparator #(.width(4)) comparator_15 (.a(OpCode), .b(4'b1110), .eq(SUBR));  // open: gt, lt
  Comparator #(.width(4)) comparator_16 (.a(OpCode), .b(4'b1111), .eq(SUBI));  // open: gt, lt
  or or_1 (or_1_out, ANDR, ANDI);
  or or_2 (or_2_out, ORR, ORI);
  or or_3 (or_3_out, XORR, XORI);
  or or_4 (or_4_out, ADDR, ADDI);
  or or_5 (or_5_out, SUBR, SUBI);
  or or_6 (or_6_out, StopTrue, NOP);
  not not_1 (IsWrite, or_6_out);
  or or_7 (IsImmediateOut, ANDI, ORI, XORI, ADDI, SUBI);
  OpLogic oplogic_1 (
    .ANDG(or_1_out), .ORG(or_2_out), .XORG(or_3_out), .NOTG(NOTInst), .NEGATEG(NEGATE), .ADDG(or_4_out),
    .SUBG(or_5_out), .ALUOP(ALU_OP_CHOICE_OUT));
  not not_2 (Stop, StopTrue);

  // Other names for the same wires on the sheet: LOAD = LOADOUT; STOP_t = StopTrue

  // Notes on the sheet:
  //   Make path for when AND, OR ,etc type instructions and somehow final is 3 bits so ALU can chosoe
  //   Make path for I type instruction, so when its I type we choose immediate, some combinational logic
endmodule

module OpLogic (
  input  ANDG,
  input  ORG,
  input  XORG,
  input  NOTG,
  input  NEGATEG,
  input  ADDG,
  input  SUBG,
  output [2:0] ALUOP
);

  wire not_1_out, not_2_out, not_3_out, not_4_out, not_5_out, not_6_out, not_7_out;

  not not_1 (not_1_out, ANDG);
  not not_2 (not_2_out, ORG);
  not not_3 (not_3_out, XORG);
  not not_4 (not_4_out, NOTG);
  not not_5 (not_5_out, NEGATEG);
  not not_6 (not_6_out, ADDG);
  not not_7 (not_7_out, SUBG);
  and and_1 (ALUOP[2], not_1_out, not_2_out, not_3_out, not_4_out);
  and and_2 (ALUOP[1], not_1_out, not_2_out, not_5_out, not_6_out);
  and and_3 (ALUOP[0], not_1_out, not_3_out, not_5_out, not_7_out);
endmodule
