// Logisim project Cache.circ as structural Verilog: 8 circuits, main circuit implementation
module implementation (
  input  [9:0] CpuAddressIn,
  input  CpuReadIn,
  input  CpuWriteIn,
  input  [7:0] CpuWriteValueIn,
  input  [31:0] LineFromMemIn,
  input  ClkIn,
  output ReadyOut,
  output DidContainOut,
  output [7:0] ByteReadOut,
  output [7:0] MemAddressOut,
  output MemReadOut,
  output MemWriteOut,
  output [31:0] Line2MemOut
);

  wire Con_Out_S0, Con_Out_S1, Dirty, DoesContain, EnableSet0, EnableSet1, Evict, FeedFSMDirty, Init,
       IsOldestDirtyS0, IsOldestDirtyS1, Miss, RCpuRead, RCpuWrite, ReadFMemory, RSet, UpdateAge, UpdateDC,
       UpdateDirty, UpdateTag, UpdateValid, Valid;
  wire [1:0] Offset;
  wire [3:0] FSMNextState_nextstate, State;
  wire [6:0] RTag;
  wire [7:0] DirtyAddressS0, DirtyAddressS1, FinalDirtyAddress, IfReadFromMem, multiplexer_1_out,
       multiplexer_7_out, multiplexer_9_out, RCpuWriteValue, Val_S0, Val_S1;
  wire [9:0] RCpuAddress;
  wire [31:0] DirtyBlockS0, DirtyBlockS1;

  // Probe on State
  Register #(.width(1)) register_1 (.D(DoesContain), .en(UpdateDC), .clk(ClkIn), .Q(DidContainOut));  // open: clr
  CurrInstruction currinstruction_1 (
    .CPU_Address(CpuAddressIn), .CPURead_in(CpuReadIn), .CPUWrite_in(CpuWriteIn),
    .CPU_Write_val_in(CpuWriteValueIn), .Ready(ReadyOut), .Clk(ClkIn), .RealCpuAddress(RCpuAddress),
    .tag(RTag), .set(RSet), .offset(Offset), .CpuRead(RCpuRead), .CpuWrite(RCpuWrite),
    .CpuWriteValue(RCpuWriteValue));
  Set Set0 (
    .Cpu_Tag(RTag), .Initialize(Init), .Clk(ClkIn), .Cpu_Offset(Offset), .CpuReadIn(RCpuRead),
    .CpuWriteIn(RCpuWrite), .CpuWriteValue(CpuWriteValueIn), .LineFromMemin(LineFromMemIn),
    .Enable(EnableSet0), .SetNUM(1'b0), .UpdateAge(UpdateAge), .UpdateTag(UpdateTag), .Valid(Valid),
    .UpdateValid(UpdateValid), .Dirty(Dirty), .UpdateDirty(UpdateDirty), .Miss(Miss), .Evict(Evict),
    .ReadFMemory(ReadFMemory), .ContainsOut(Con_Out_S0), .ContainsVAL(Val_S0),
    .DirtyValofOldest(IsOldestDirtyS0), .DirtyWriteOut(DirtyAddressS0), .DirtyBlockOut(DirtyBlockS0));
  Set Set1 (
    .Cpu_Tag(RTag), .Initialize(Init), .Clk(ClkIn), .Cpu_Offset(Offset), .CpuReadIn(RCpuRead),
    .CpuWriteIn(RCpuWrite), .CpuWriteValue(CpuWriteValueIn), .LineFromMemin(LineFromMemIn),
    .Enable(EnableSet1), .SetNUM(1'b1), .UpdateAge(UpdateAge), .UpdateTag(UpdateTag), .Valid(Valid),
    .UpdateValid(UpdateValid), .Dirty(Dirty), .UpdateDirty(UpdateDirty), .Miss(Miss), .Evict(Evict),
    .ReadFMemory(ReadFMemory), .ContainsOut(Con_Out_S1), .ContainsVAL(Val_S1),
    .DirtyValofOldest(IsOldestDirtyS1), .DirtyWriteOut(DirtyAddressS1), .DirtyBlockOut(DirtyBlockS1));
  Multiplexer #(.enable("false"), .width(8)) multiplexer_1 (
    .in0(Val_S0), .in1(Val_S1), .out(multiplexer_1_out), .sel(RSet));
  Demultiplexer #(.enable("false")) demultiplexer_1 (.out0(EnableSet0), .out1(EnableSet1), .in(1'b1), .sel(RSet));
  Multiplexer #(.enable("false")) multiplexer_2 (.in0(Con_Out_S0), .in1(Con_Out_S1), .out(DoesContain), .sel(RSet));
  Multiplexer #(.enable("false"), .width(8)) multiplexer_3 (
    .in1({RTag, RSet}), .out(IfReadFromMem), .sel(MemReadOut));  // open: in0
  Multiplexer #(.enable("false"), .width(8)) multiplexer_4 (
    .in0(DirtyAddressS0), .in1(DirtyAddressS1), .out(FinalDirtyAddress), .sel(RSet));
  Multiplexer #(.enable("false")) multiplexer_5 (
    .in0(IsOldestDirtyS0), .in1(IsOldestDirtyS1), .out(FeedFSMDirty), .sel(RSet));
  Multiplexer #(.enable("false"), .width(32)) multiplexer_6 (
    .in0(DirtyBlockS0), .in1(DirtyBlockS1), .out(Line2MemOut), .sel(RSet));
  Multiplexer #(.enable("false"), .width(8)) multiplexer_7 (
    .in0({8{1'b0}}), .in1(multiplexer_1_out), .out(multiplexer_7_out), .sel(DoesContain));
  FSM FSMNextState (
    .StateIn(State), .DidContain(DoesContain), .Dirty(FeedFSMDirty), .Read(RCpuRead), .Write(RCpuWrite),
    .NextState(FSMNextState_nextstate));
  Multiplexer #(.enable("false"), .width(8)) multiplexer_8 (
    .in0({8{1'b0}}), .in1(multiplexer_7_out), .out(ByteReadOut), .sel(RCpuRead));
  Register #(.width(4)) register_2 (.D(FSMNextState_nextstate), .clk(ClkIn), .Q(State));  // open: en, clr
  // Probe on State
  Multiplexer #(.enable("false"), .width(8)) multiplexer_9 (
    .in1(IfReadFromMem), .out(multiplexer_9_out), .sel(MemReadOut));  // open: in0
  Multiplexer #(.enable("false"), .width(8)) multiplexer_10 (
    .in0(multiplexer_9_out), .in1(FinalDirtyAddress), .out(MemAddressOut), .sel(MemWriteOut));
  FSMOut fsmout_1 (
    .State(State), .Initialize(Init), .Ready(ReadyOut), .Valid(Valid), .UpdateValid(UpdateValid),
    .UpdateTag(UpdateTag), .Evict(Evict), .Miss(Miss), .Dirty(Dirty), .UpdateDirty(UpdateDirty),
    .MemReadReq(MemReadOut), .MemWriteReq(MemWriteOut), .ReadFromMemory(ReadFMemory), .UpdateAge(UpdateAge),
    .UpdateDC(UpdateDC));

  // Other names for the same wires on the sheet: clk = ClkIn; CpuAddress[9:0] = CpuAddressIn; CpuRead = CpuReadIn;
  //   CpuWrite = CpuWriteIn; CpuWriteValue[7:0] = CpuWriteValueIn; DidContain = DidContainOut;
  //   LineFromMem[31:0] = LineFromMemIn; MemAddress[7:0] = MemAddressOut; MemRead = MemReadOut;
  //   MemWrite = MemWriteOut; ByteRead[7:0] = ByteReadOut; SelectedSetByteRead[7:0] = ByteReadOut;
  //   Line2Mem[31:0] = Line2MemOut; SelectedSetLine2Mem[31:0] = Line2MemOut; Ready = ReadyOut; TempReady = ReadyOut

  // Notes on the sheet:
  //   After hit cases work with Age + Initialize
  //   R for real
  //   Storing Values, Only changse when Ready =1
  //   Update in decode stage
  //   Read With Cache hit --> Write with Cache hit --> Read with Cache Miss --> Write with Cache Miss --> FSM
  //   Assume the very instance i set mem read to 1 I get the value 
  //   Then Give input the Line2Mem
  //   Logic For our Enable Age
  //   Did Contain Logic
  //   Even if neither contains it will be 0, can be used for both read/write
  //   If it does contain return value, otherwise 0 (and also it's read, write doesnt return value
  //   Set miss from FSM because when we do not contain, we give the output the mem address we want to read from
  //   Logic for When Missing, so when it does not contain: set mem read to 1
  //   But we have to see if its dirty or not first, put condition here
  //   For Miss then read in FSM, set dirty to 0, valid to 1 , Renew tag 
  //   At the enable tag maybe or gate
  //   If initializing probably overwrite Enable logic
  //   Basically used for enabling the whole set 
  //   Different cases like Enable and write then bla bla
  //   If Read MemAddress is Basically Tag +offset , if mem write ,return tag+offset from oldest way that is dirty
  //   Do Rset thing if dirty is 1 then write to mem address when evict
  //   Assume we have FSM Set output accordingly
  //   correct value 
  //   Case when eviction is true
  //   Regardless, if we're at final stage of read then did contain should give 
  //   and next cyclewhen ready = 1 should be correct 
endmodule

module Set (
  input  [6:0] Cpu_Tag,
  input  Initialize,
  input  Clk,
  input  [1:0] Cpu_Offset,
  input  CpuReadIn,
  input  CpuWriteIn,
  input  [7:0] CpuWriteValue,
  input  [31:0] LineFromMemin,
  input  Enable,
  input  SetNUM,
  input  UpdateAge,
  input  UpdateTag,
  input  Valid,
  input  UpdateValid,
  input  Dirty,
  input  UpdateDirty,
  input  Miss,
  input  Evict,
  input  ReadFMemory,
  output ContainsOut,
  output [7:0] ContainsVAL,
  output DirtyValofOldest,
  output [7:0] DirtyWriteOut,
  output [31:0] DirtyBlockOut
);

  wire and_3_out, and_4_out, and_5_out, and_6_out, and_7_out, and_8_out, and_9_out, and_10_out, and_11_out,
       and_12_out, and_13_out, and_14_out, DoRead, DoWrite, multiplexer_8_out, multiplexer_13_out, OldestM0,
       OldestM1, OldestM2, W0Contain, W0Dirty, W1Contain, W1Dirty, W2Contain, W2Dirty;
  wire [1:0] multiplexer_4_out, multiplexer_5_out, multiplexer_6_out, multiplexer_7_out, W0Age, W0NA,
       W0NextAge, W1Age, W1NA, W1NextAge, W2Age, W2NA, W2NextAge;
  wire [7:0] AddressW0, AddressW1, AddressW2, multiplexer_9_out, multiplexer_11_out, multiplexer_12_out,
       multiplexer_14_out, W0Val, W1Val, W2Val;
  wire [31:0] BlockOutW0, BlockOutW1, BlockOutW2, multiplexer_10_out, multiplexer_15_out, undriven;

  Multiplexer #(.enable("false"), .width(2)) multiplexer_1 (.in0(W0NextAge), .in1(2'b00), .out(W0NA), .sel(Initialize));
  Multiplexer #(.enable("false"), .width(2)) multiplexer_2 (.in0(W1NextAge), .in1(2'b01), .out(W1NA), .sel(Initialize));
  Multiplexer #(.enable("false"), .width(2)) multiplexer_3 (.in0(W2NextAge), .in1(2'b10), .out(W2NA), .sel(Initialize));
  Multiplexer #(.enable("false"), .width(2)) multiplexer_4 (
    .in0(2'b00), .in1(W0Age), .out(multiplexer_4_out), .sel(W0Contain));
  Multiplexer #(.enable("false"), .width(2)) multiplexer_5 (
    .in0(multiplexer_4_out), .in1(W1Age), .out(multiplexer_5_out), .sel(W1Contain));
  and and_1 (DoRead, CpuReadIn, Enable);
  and and_2 (DoWrite, CpuWriteIn, Enable);
  Multiplexer #(.enable("false"), .width(2)) multiplexer_6 (
    .in0(multiplexer_5_out), .in1(W2Age), .out(multiplexer_6_out), .sel(W2Contain));
  and and_3 (and_3_out, OldestM0, Enable);
  and and_4 (and_4_out, OldestM2, Enable);
  and and_5 (and_5_out, OldestM1, Enable);
  Multiplexer #(.enable("false"), .width(2)) multiplexer_7 (
    .in0(2'b10), .in1(multiplexer_6_out), .out(multiplexer_7_out), .sel(ContainsOut));
  NextAge nextage_1 (
    .AgeW0(W0Age), .AgeW1(W1Age), .AgeW2(W2Age), .CurrentAge(multiplexer_7_out), .NextAgeW0(W0NextAge),
    .NextAgeW1(W1NextAge), .NextAgeW2(W2NextAge));
  Ways Way0 (
    .Cpu_Tag(Cpu_Tag), .Clk(Clk), .Cpu_Offset(Cpu_Offset), .CpuReadIn(DoRead), .CpuWriteIn(DoWrite),
    .CpuWriteValue(CpuWriteValue), .LineFromMemin(LineFromMemin), .UpdateAge(UpdateAge), .NextAge(W0NA),
    .UpdateTag(UpdateTag), .UpdateValid(UpdateValid), .UpdateDirty(UpdateDirty), .Miss(Miss),
    .Enable(Enable), .IsOldestAge(and_3_out), .ReadFMem(ReadFMemory), .Valid(Valid), .Dirty(Dirty),
    .Evict(Evict), .Initialize(Initialize), .SetNum(SetNUM), .ContainsOut(W0Contain), .ContainValue(W0Val),
    .Dirty_out(W0Dirty), .Ages(W0Age), .MemWriteOutAddress(AddressW0), .BlockWriteOut(BlockOutW0));
  Ways Way1 (
    .Cpu_Tag(Cpu_Tag), .Clk(Clk), .Cpu_Offset(Cpu_Offset), .CpuReadIn(DoRead), .CpuWriteIn(DoWrite),
    .CpuWriteValue(CpuWriteValue), .LineFromMemin(LineFromMemin), .UpdateAge(UpdateAge), .NextAge(W1NA),
    .UpdateTag(UpdateTag), .UpdateValid(UpdateValid), .UpdateDirty(UpdateDirty), .Miss(Miss),
    .Enable(Enable), .IsOldestAge(and_5_out), .ReadFMem(ReadFMemory), .Valid(Valid), .Dirty(Dirty),
    .Evict(Evict), .Initialize(Initialize), .SetNum(SetNUM), .ContainsOut(W1Contain), .ContainValue(W1Val),
    .Dirty_out(W1Dirty), .Ages(W1Age), .MemWriteOutAddress(AddressW1), .BlockWriteOut(BlockOutW1));
  Ways Way2 (
    .Cpu_Tag(Cpu_Tag), .Clk(Clk), .Cpu_Offset(Cpu_Offset), .CpuReadIn(DoRead), .CpuWriteIn(DoWrite),
    .CpuWriteValue(CpuWriteValue), .LineFromMemin(LineFromMemin), .UpdateAge(UpdateAge), .NextAge(W2NA),
    .UpdateTag(UpdateTag), .UpdateValid(UpdateValid), .UpdateDirty(UpdateDirty), .Miss(Miss),
    .Enable(Enable), .IsOldestAge(and_4_out), .ReadFMem(ReadFMemory), .Valid(Valid), .Dirty(Dirty),
    .Evict(Evict), .Initialize(Initialize), .SetNum(SetNUM), .ContainsOut(W2Contain), .ContainValue(W2Val),
    .Dirty_out(W2Dirty), .Ages(W2Age), .MemWriteOutAddress(AddressW2), .BlockWriteOut(BlockOutW2));
  and and_6 (and_6_out, W0Dirty, OldestM0);
  Multiplexer #(.enable("false")) multiplexer_8 (.in0(1'b0), .in1(1'b1), .out(multiplexer_8_out), .sel(and_6_out));
  and and_7 (and_7_out, W0Dirty, OldestM0);
  Multiplexer #(.enable("false"), .width(8)) multiplexer_9 (
    .in0({8{1'b0}}), .in1(AddressW0), .out(multiplexer_9_out), .sel(and_7_out));
  and and_8 (and_8_out, W0Dirty, OldestM0);
  Multiplexer #(.enable("false"), .width(32)) multiplexer_10 (
    .in0(undriven), .in1(BlockOutW0), .out(multiplexer_10_out), .sel(and_8_out));
  Multiplexer #(.enable("false"), .width(8)) multiplexer_11 (
    .in0({8{1'b0}}), .in1(W0Val), .out(multiplexer_11_out), .sel(W0Contain));
  and and_9 (and_9_out, W1Dirty, OldestM1);
  or or_1 (ContainsOut, W0Contain, W1Contain, W2Contain);
  Multiplexer #(.enable("false"), .width(8)) multiplexer_12 (
    .in0(multiplexer_11_out), .in1(W1Val), .out(multiplexer_12_out), .sel(W1Contain));
  Multiplexer #(.enable("false")) multiplexer_13 (
    .in0(multiplexer_8_out), .in1(1'b1), .out(multiplexer_13_out), .sel(and_9_out));
  and and_10 (and_10_out, W1Dirty, OldestM1);
  Multiplexer #(.enable("false"), .width(8)) multiplexer_14 (
    .in0(multiplexer_9_out), .in1(AddressW1), .out(multiplexer_14_out), .sel(and_10_out));
  and and_11 (and_11_out, W1Dirty, OldestM1);
  Multiplexer #(.enable("false"), .width(32)) multiplexer_15 (
    .in0(multiplexer_10_out), .in1(BlockOutW1), .out(multiplexer_15_out), .sel(and_11_out));
  Comparator #(.mode("unsigned"), .width(2)) comparator_1 (.a(W0Age), .b(2'b10), .eq(OldestM0));  // open: gt, lt
  Comparator #(.mode("unsigned"), .width(2)) comparator_2 (.a(W1Age), .b(2'b10), .eq(OldestM1));  // open: gt, lt
  Comparator #(.mode("unsigned"), .width(2)) comparator_3 (.a(W2Age), .b(2'b10), .eq(OldestM2));  // open: gt, lt
  Multiplexer #(.enable("false"), .width(8)) multiplexer_16 (
    .in0(multiplexer_12_out), .in1(W2Val), .out(ContainsVAL), .sel(W2Contain));
  and and_12 (and_12_out, W2Dirty, OldestM2);
  Multiplexer #(.enable("false")) multiplexer_17 (
    .in0(multiplexer_13_out), .in1(1'b1), .out(DirtyValofOldest), .sel(and_12_out));
  and and_13 (and_13_out, W2Dirty, OldestM2);
  Multiplexer #(.enable("false"), .width(8)) multiplexer_18 (
    .in0(multiplexer_14_out), .in1(AddressW2), .out(DirtyWriteOut), .sel(and_13_out));
  and and_14 (and_14_out, W2Dirty, OldestM2);
  Multiplexer #(.enable("false"), .width(32)) multiplexer_19 (
    .in0(multiplexer_15_out), .in1(BlockOutW2), .out(DirtyBlockOut), .sel(and_14_out));

  // Other names for the same wires on the sheet: ContainedVal[7:0] = ContainsVAL; CpuWriteVal[7:0] = CpuWriteValue;
  //   Did_Contain = ContainsOut; FinalDirty = DirtyValofOldest; Init = Initialize; IsEnabled = Enable;
  //   IsRead = CpuReadIn; IsWrite = CpuWriteIn; LineFMem[31:0] = LineFromMemin; Offset[1:0] = Cpu_Offset;
  //   Tag[6:0] = Cpu_Tag

  // Notes on the sheet:
  //   Update Age Logic:
  //   For Age there is enable inside
  //   But init overrides it
  //   Make sure we want to only update age at the very end
  //   If we hit or miss, hvae to be careful, we dont want age to change again if..
  //   Use the input called UpdateAge as enable
  //   Dont think this is right, because if we miss then we didnt contain, so we bring in from memory, but then it will become did contain: True so we change age again which we shoudnt
  //   This is where Update Age comes in, Do we want to update age in the first place?
  //   Change inside to nextage
  //   Curent Age: If we have a hit in way 0 then i want to set currAge to whatever AgeW0 is 
  //   Two Cases when we hit, then Curr Age is age of that way we hit
  //   If cache miss, we evict oldest block and set curr age to 10 since oldest is always that
  //   Then internally we use it to compare, muxes etc to current age
  //   The did contain Inside this circuit actually is Does_countain/ Not to be confused with wordings outside
  //   By logic only one can be the oldest and we see if it is dirty or not if both Oldest and Dirty then it will return 0
  //   So on the outside we dont need to recalculate logic of if the way we have is the oldest
  //   Either W0 W1 or W2 will contain it otherwise 0
  //   Evict Logic 2 Cases If dirty or if not dirty
  //   1. If we miss, we look at which one has oldest age
  //   Probably pre calculated
  //   So we keep track of which way it is so we can send it Miss = 1 
  //   Well we evict only if we miss so there's that 
  //   2.If Miss| Evict | oldest + dirty|Enable
  //   For our purposes oldest way is always age 2 
  //   which ever one has age = 2 we use that way to read from memory
  //   so when evict =1 miss =1
  //   If the oldest one is dirty
endmodule

module Ways (
  input  [6:0] Cpu_Tag,
  input  Clk,
  input  [1:0] Cpu_Offset,
  input  CpuReadIn,
  input  CpuWriteIn,
  input  [7:0] CpuWriteValue,
  input  [31:0] LineFromMemin,
  input  UpdateAge,
  input  [1:0] NextAge,
  input  UpdateTag,
  input  UpdateValid,
  input  UpdateDirty,
  input  Miss,
  input  Enable,
  input  IsOldestAge,
  input  ReadFMem,
  input  Valid,
  input  Dirty,
  input  Evict,
  input  Initialize,
  input  SetNum,
  output ContainsOut,
  output [7:0] ContainValue,
  output Dirty_out,
  output [1:0] Ages,
  output [7:0] MemWriteOutAddress,
  output [31:0] BlockWriteOut
);

  wire and_1_out, and_2_out, and_3_out, and_4_out, and_5_out, and_6_out, and_7_out, and_8_out, and_9_out,
       and_10_out, ByteChange, comparator_1_eq, or_1_out, Valid_dat_out;
  wire [7:0] multiplexer_1_out, multiplexer_2_out, multiplexer_3_out, multiplexer_4_out, multiplexer_5_out,
       multiplexer_6_out, multiplexer_7_out, multiplexer_8_out, multiplexer_9_out;

  and and_1 (and_1_out, Enable, IsOldestAge, UpdateTag, Evict);
  and and_2 (and_2_out, Enable, IsOldestAge, UpdateValid, Evict);
  Register #(.width(7)) Tag_dat (.D(Cpu_Tag), .en(and_1_out), .clk(Clk), .Q(MemWriteOutAddress[7:1]));  // open: clr
  Register #(.width(1)) Valid_dat (.D(Valid), .en(and_2_out), .clk(Clk), .Q(Valid_dat_out));  // open: clr
  Multiplexer #(.enable("false"), .select(2), .width(8)) multiplexer_1 (
    .in0(CpuWriteValue), .in1(BlockWriteOut[7:0]), .in2(BlockWriteOut[7:0]), .in3(BlockWriteOut[7:0]),
    .out(multiplexer_1_out), .sel(Cpu_Offset));
  Multiplexer #(.enable("false"), .select(2), .width(8)) multiplexer_2 (
    .in0(BlockWriteOut[15:8]), .in1(CpuWriteValue), .in2(BlockWriteOut[15:8]), .in3(BlockWriteOut[15:8]),
    .out(multiplexer_2_out), .sel(Cpu_Offset));
  Multiplexer #(.enable("false"), .select(2), .width(8)) multiplexer_3 (
    .in0(BlockWriteOut[23:16]), .in1(BlockWriteOut[23:16]), .in2(CpuWriteValue), .in3(BlockWriteOut[23:16]),
    .out(multiplexer_3_out), .sel(Cpu_Offset));
  Multiplexer #(.enable("false"), .select(2), .width(8)) multiplexer_4 (
    .in0(BlockWriteOut[31:24]), .in1(BlockWriteOut[31:24]), .in2(BlockWriteOut[31:24]), .in3(CpuWriteValue),
    .out(multiplexer_4_out), .sel(Cpu_Offset));
  and and_3 (and_3_out, Enable, ByteChange);
  Multiplexer #(.enable("false"), .width(8)) multiplexer_5 (
    .in0(multiplexer_1_out), .in1(LineFromMemin[7:0]), .out(multiplexer_5_out), .sel(Miss));
  and and_4 (and_4_out, Enable, ByteChange);
  Multiplexer #(.enable("false"), .width(8)) multiplexer_6 (
    .in0(multiplexer_2_out), .in1(LineFromMemin[15:8]), .out(multiplexer_6_out), .sel(Miss));
  Register Byte1_dat (.D(multiplexer_6_out), .en(and_5_out), .clk(Clk), .Q(BlockWriteOut[15:8]));  // open: clr
  and and_5 (and_5_out, Enable, ByteChange);
  Multiplexer #(.enable("false"), .width(8)) multiplexer_7 (
    .in0(multiplexer_3_out), .in1(LineFromMemin[23:16]), .out(multiplexer_7_out), .sel(Miss));
  Register Byte2_dat (.D(multiplexer_7_out), .en(and_6_out), .clk(Clk), .Q(BlockWriteOut[23:16]));  // open: clr
  and and_6 (and_6_out, Enable, ByteChange);
  Multiplexer #(.enable("false"), .width(8)) multiplexer_8 (
    .in0(multiplexer_4_out), .in1(LineFromMemin[31:24]), .out(multiplexer_8_out), .sel(Miss));
  Register Byte3_dat (.D(multiplexer_8_out), .en(and_3_out), .clk(Clk), .Q(BlockWriteOut[31:24]));  // open: clr
  Register Byte0_dat (.D(multiplexer_5_out), .en(and_4_out), .clk(Clk), .Q(BlockWriteOut[7:0]));  // open: clr
  and and_7 (and_7_out, Enable, UpdateAge);
  and and_8 (and_8_out, ContainsOut, CpuWriteIn);
  and and_9 (and_9_out, Enable, IsOldestAge, UpdateDirty);
  or or_1 (or_1_out, and_7_out, Initialize);
  or or_2 (ByteChange, and_8_out, and_10_out);
  and and_10 (and_10_out, ReadFMem, IsOldestAge, Evict);
  Register #(.width(1)) Dirty_dat (.D(Dirty), .en(and_9_out), .clk(Clk), .Q(Dirty_out));  // open: clr
  Register #(.width(2)) Age_dat (.D(NextAge), .en(or_1_out), .clk(Clk), .Q(Ages));  // open: clr
  Multiplexer #(.enable("false"), .select(2), .width(8)) multiplexer_9 (
    .in0(BlockWriteOut[7:0]), .in1(BlockWriteOut[15:8]), .in2(BlockWriteOut[23:16]),
    .in3(BlockWriteOut[31:24]), .out(multiplexer_9_out), .sel(Cpu_Offset));
  Comparator #(.width(7)) comparator_1 (
    .a(Cpu_Tag), .b(MemWriteOutAddress[7:1]), .eq(comparator_1_eq));  // open: gt, lt
  Multiplexer #(.enable("false"), .width(8)) multiplexer_10 (
    .in0({8{1'b0}}), .in1(multiplexer_9_out), .out(ContainValue), .sel(ContainsOut));
  and and_11 (ContainsOut, comparator_1_eq, Valid_dat_out);
  // Probe on {MemWriteOutAddress[7:1], SetNum}

  assign MemWriteOutAddress[0] = SetNum;

  // Other names for the same wires on the sheet: Age_dat_out[1:0] = Ages; Byte0_out[7:0] = BlockWriteOut[7:0];
  //   Byte1_out[7:0] = BlockWriteOut[15:8]; Byte2_out[7:0] = BlockWriteOut[23:16];
  //   Byte3_out[7:0] = BlockWriteOut[31:24]; Contain_Val[7:0] = ContainValue; Dirty_dat_out = Dirty_out;
  //   Does_Contain = ContainsOut; Init = Initialize; IsEnable = Enable; IsRead = CpuReadIn; IsWrite = CpuWriteIn;
  //   Byte0[7:0] = LineFromMemin[7:0]; LFromM[31:0] = LineFromMemin; Byte1[7:0] = LineFromMemin[15:8];
  //   Byte2[7:0] = LineFromMemin[23:16]; Byte3[7:0] = LineFromMemin[31:24];
  //   Tag_dat_Out[6:0] = MemWriteOutAddress[7:1]; ReadFMemory = ReadFMem; WriteValue[7:0] = CpuWriteValue

  // Notes on the sheet:
  //   Dont need this
  //   **Write When Hit Logic**
  //   We write to indivdual byte if it contained 
  //   What will Happen When we want to evict?
  //   Make muxes to choose when to evict
  //   First calculate oldest age then use muxes to choose it
  //   When it is evict, which is probably chosen by fsm if dirty write back
  //   Change to is write or read from memory
  //   Not Sure but when do we read from memory?
  //   when it does not contain and we evict?
  //   Bytes Change control
  //   From FSM?
  //   Or when we read from memory and we change the whole block
  //   Yea bytes only change when we write or read from memory
  //   If this way does contain and it is write then we change to 1
  //   We only change it when, it contains same tag and is write then we write there
  //   Is oldest already controlled by ecivt outside
  //   Only byte change the one that is oldest
  //   If we read from mem dirty = 0
  //   As soon as we write dirty = 1
  //   Compare to see if contains and valid = hit
  //   If Our Way Contains the value look at the Offset to see which Byte we look at 
  //   But how would FSM help enable this
  //   Like when do we choose to update dirty
  //   Otherwise if its not, we go to the case where we just bring stuff in from mem giving address
  //   Either we find Logic for Dirty or directly Use fsm to tell what dirty is
  //   Go through logic of which one is largest again
  //   Give out dirty here and give out LIne mem 
  //   In sets if it is dirty and oldest age and is evict then we return it back
  //   Used for comparing age outside in set
endmodule

module CurrInstruction (
  input  [9:0] CPU_Address,
  input  CPURead_in,
  input  CPUWrite_in,
  input  [7:0] CPU_Write_val_in,
  input  Ready,
  input  Clk,
  output [9:0] RealCpuAddress,
  output [6:0] tag,
  output set,
  output [1:0] offset,
  output CpuRead,
  output CpuWrite,
  output [7:0] CpuWriteValue
);

  Register #(.width(2)) register_1 (.D(CPU_Address[1:0]), .en(Ready), .clk(Clk), .Q(offset));  // open: clr
  Register #(.width(1)) register_2 (.D(CPU_Address[2]), .en(Ready), .clk(Clk), .Q(set));  // open: clr
  Register #(.width(1)) register_3 (.D(CPUWrite_in), .en(Ready), .clk(Clk), .Q(CpuWrite));  // open: clr
  Register #(.width(10)) cpu_acaddress (.D(CPU_Address), .en(Ready), .clk(Clk));  // open: Q, clr
  Register #(.width(7)) register_4 (.D(CPU_Address[9:3]), .en(Ready), .clk(Clk), .Q(tag));  // open: clr
  Register #(.width(1)) register_5 (.D(CPURead_in), .en(Ready), .clk(Clk), .Q(CpuRead));  // open: clr
  Register register_6 (.D(CPU_Write_val_in), .en(Ready), .clk(Clk), .Q(CpuWriteValue));  // open: clr

  // Other names for the same wires on the sheet: CpuAddress[9:0] = CPU_Address; offset_bits[1:0] = CPU_Address[1:0];
  //   set_bits = CPU_Address[2]; tag_bits[6:0] = CPU_Address[9:3]; CpuRead_t = CPURead_in; CpuWrite_t = CPUWrite_in;
  //   CpuWriteValue_t[7:0] = CPU_Write_val_in; Real_cpuAddress[9:0] = RealCpuAddress; real_offset[1:0] = offset;
  //   real_read = CpuRead; real_set = set; real_tag[6:0] = tag; real_write = CpuWrite;
  //   real_write_value[7:0] = CpuWriteValue

  // Notes on the sheet:
  //   Would only ever be valid if ready is 1
  //   Didnt use this -->
endmodule

module NextAge (
  input  [1:0] AgeW0,
  input  [1:0] AgeW1,
  input  [1:0] AgeW2,
  input  [1:0] CurrentAge,
  output [1:0] NextAgeW0,
  output [1:0] NextAgeW1,
  output [1:0] NextAgeW2
);

  wire [1:0] adder_1_out, adder_2_out, adder_3_out;
  wire [2:0] ChooseAW0, ChooseAW1, ChooseAW2;

  Comparator #(.mode("unsigned"), .width(2)) comparator_1 (
    .a(AgeW0), .b(CurrentAge), .gt(ChooseAW0[2]), .eq(ChooseAW0[1]), .lt(ChooseAW0[0]));
  Comparator #(.mode("unsigned"), .width(2)) comparator_2 (
    .a(AgeW1), .b(CurrentAge), .gt(ChooseAW1[2]), .eq(ChooseAW1[1]), .lt(ChooseAW1[0]));
  Comparator #(.mode("unsigned"), .width(2)) comparator_3 (
    .a(AgeW2), .b(CurrentAge), .gt(ChooseAW2[2]), .eq(ChooseAW2[1]), .lt(ChooseAW2[0]));
  // Probe on ChooseAW0
  // Probe on ChooseAW1
  // Probe on ChooseAW2
  Adder #(.width(2)) adder_1 (.a(AgeW0), .b(2'b01), .out(adder_1_out));  // open: cin, cout
  Adder #(.width(2)) adder_2 (.a(AgeW1), .b(2'b01), .out(adder_2_out));  // open: cin, cout
  Adder #(.width(2)) adder_3 (.a(AgeW2), .b(2'b01), .out(adder_3_out));  // open: cin, cout
  // Probe on NextAgeW0
  Multiplexer #(.enable("false"), .select(3), .width(2)) multiplexer_1 (
    .in1(adder_1_out), .in2(2'b00), .in4(AgeW0), .out(NextAgeW0), .sel(ChooseAW0));  // open: in0, in3, in5, in6, in7
  // Probe on NextAgeW1
  Multiplexer #(.enable("false"), .select(3), .width(2)) multiplexer_2 (
    .in1(adder_2_out), .in2(2'b00), .in4(AgeW1), .out(NextAgeW1), .sel(ChooseAW1));  // open: in0, in3, in5, in6, in7
  // Probe on NextAgeW2
  Multiplexer #(.enable("false"), .select(3), .width(2)) multiplexer_3 (
    .in1(adder_3_out), .in2(2'b00), .in4(AgeW2), .out(NextAgeW2), .sel(ChooseAW2));  // open: in0, in3, in5, in6, in7

  // Other names for the same wires on the sheet: AW0[1:0] = AgeW0; AW1[1:0] = AgeW1; AW2[1:0] = AgeW2;
  //   CurrAge[1:0] = CurrentAge; NextAW0[1:0] = NextAgeW0; NextAW1[1:0] = NextAgeW1; NextAW2[1:0] = NextAgeW2

  // Notes on the sheet:
  //   Remember to use unsigned
  //   For comparators here remember to use unsigned when comparing greater less than... check
  //   Choose will always be either of 3 cases
  //   Top: < Middle = Bottom >
endmodule

module FSM (
  input  [3:0] StateIn,
  input  DidContain,
  input  Dirty,
  input  Read,
  input  Write,
  output [3:0] NextState
);

  wire and_1_out, and_2_out, and_3_out, and_4_out, and_5_out, and_6_out, and_7_out, and_8_out, and_9_out,
       and_10_out, and_11_out, and_12_out, and_13_out, and_14_out, and_15_out, and_16_out, and_17_out,
       and_18_out, and_19_out, and_20_out, and_21_out, and_22_out, not_1_out, not_2_out, not_3_out,
       not_4_out, not_5_out, not_6_out, not_7_out, not_8_out;

  not not_1 (not_1_out, StateIn[3]);
  not not_2 (not_2_out, StateIn[2]);
  not not_3 (not_3_out, StateIn[1]);
  not not_4 (not_4_out, StateIn[0]);
  not not_5 (not_5_out, DidContain);
  not not_6 (not_6_out, Dirty);
  not not_7 (not_7_out, Read);
  not not_8 (not_8_out, Write);
  and and_1 (and_1_out, StateIn[2], not_3_out, StateIn[0], Dirty);
  and and_2 (and_2_out, StateIn[2], StateIn[1], not_4_out, not_7_out);
  and and_3 (and_3_out, StateIn[3], not_3_out, StateIn[0]);
  and and_4 (and_4_out, StateIn[3], StateIn[1], not_4_out);
  and and_5 (and_5_out, not_1_out, not_2_out, StateIn[1], not_4_out, not_5_out);
  and and_6 (and_6_out, not_2_out, StateIn[1], not_4_out, not_6_out, not_7_out);
  and and_7 (and_7_out, not_2_out, StateIn[1], not_4_out, DidContain, not_7_out);
  and and_8 (and_8_out, StateIn[2], not_3_out, StateIn[0], not_6_out);
  and and_9 (and_9_out, StateIn[2], StateIn[1], not_4_out, not_8_out);
  and and_10 (and_10_out, not_2_out, not_3_out, StateIn[0]);
  and and_11 (and_11_out, not_3_out, StateIn[0], not_6_out);
  and and_12 (and_12_out, StateIn[1], not_4_out, DidContain, not_8_out);
  and and_13 (and_13_out, StateIn[2], StateIn[1], not_4_out, not_8_out);
  and and_14 (and_14_out, StateIn[3], StateIn[1], not_4_out, not_6_out, not_8_out);
  and and_15 (and_15_out, not_1_out, not_2_out, not_4_out, not_5_out);
  and and_16 (and_16_out, not_3_out, not_4_out);
  and and_17 (and_17_out, not_4_out, not_8_out);
  and and_18 (and_18_out, not_2_out, not_4_out, not_5_out, Read);
  and and_19 (and_19_out, not_2_out, not_4_out, not_5_out, Dirty);
  and and_20 (and_20_out, not_1_out, StateIn[1], StateIn[0]);
  and and_21 (and_21_out, not_2_out, StateIn[1], StateIn[0]);
  and and_22 (and_22_out, StateIn[2], not_3_out, Dirty);
  or or_1 (NextState[3], and_1_out, and_2_out, and_3_out, and_4_out);
  or or_2 (NextState[2], and_5_out, and_6_out, and_7_out, and_8_out, and_9_out);
  or or_3 (NextState[1], and_10_out, and_11_out, and_12_out, and_13_out, and_14_out);
  or or_4 (NextState[0], and_15_out, and_16_out, and_17_out, and_18_out, and_19_out, and_20_out, and_21_out, and_22_out);
endmodule

module FSMOut (
  input  [3:0] State,
  output Initialize,
  output Ready,
  output Valid,
  output UpdateValid,
  output UpdateTag,
  output Evict,
  output Miss,
  output Dirty,
  output UpdateDirty,
  output MemReadReq,
  output MemWriteReq,
  output ReadFromMemory,
  output UpdateAge,
  output UpdateDC
);

  wire and_3_out, and_4_out, and_5_out, and_6_out, and_7_out, and_8_out, and_9_out, and_10_out, and_11_out,
       and_12_out, and_13_out, and_14_out, and_15_out, and_16_out, and_17_out, and_18_out, and_19_out,
       and_20_out, and_21_out, and_23_out, and_24_out, and_25_out, and_26_out, and_27_out, not_1_out,
       not_2_out, not_3_out, not_4_out;

  not not_1 (not_1_out, State[3]);
  not not_2 (not_2_out, State[2]);
  not not_3 (not_3_out, State[1]);
  not not_4 (not_4_out, State[0]);
  and and_1 (Initialize, not_1_out, not_2_out, not_3_out, not_4_out);
  and and_2 (Ready, not_1_out, not_2_out, not_3_out, State[0]);
  and and_3 (and_3_out, State[1], State[0]);
  and and_4 (and_4_out, State[2], State[1], not_4_out);
  and and_5 (and_5_out, State[3], State[1], not_4_out);
  and and_6 (and_6_out, State[2], State[1], not_4_out);
  and and_7 (and_7_out, State[3], State[1], not_4_out);
  and and_8 (and_8_out, State[2], not_3_out, State[0]);
  and and_9 (and_9_out, State[2], State[1], not_4_out);
  and and_10 (and_10_out, State[3], not_3_out, State[0]);
  and and_11 (and_11_out, State[3], State[1], not_4_out);
  and and_12 (and_12_out, State[2], not_3_out, State[0]);
  and and_13 (and_13_out, State[2], State[1], not_4_out);
  and and_14 (and_14_out, State[3], not_3_out, State[0]);
  and and_15 (and_15_out, State[3], State[1], not_4_out);
  and and_16 (and_16_out, State[2], not_3_out, not_4_out);
  and and_17 (and_17_out, State[3], not_3_out);
  and and_18 (and_18_out, State[2], not_4_out);
  and and_19 (and_19_out, State[3], not_4_out);
  and and_20 (and_20_out, State[2], State[1], not_4_out);
  and and_21 (and_21_out, State[3], State[1], not_4_out);
  and and_22 (MemWriteReq, State[3], not_3_out, State[0]);
  and and_23 (and_23_out, State[2], State[1], not_4_out);
  and and_24 (and_24_out, State[3], State[1], not_4_out);
  and and_25 (and_25_out, State[1], State[0]);
  and and_26 (and_26_out, State[2], not_3_out, not_4_out);
  and and_27 (and_27_out, State[3], not_3_out, not_4_out);
  and and_28 (UpdateDC, not_1_out, not_2_out, State[1], not_4_out);
  or or_1 (Valid, and_3_out, State[2], State[3]);
  or or_2 (UpdateValid, and_4_out, and_5_out);
  or or_3 (UpdateTag, and_6_out, and_7_out);
  or or_4 (Evict, and_8_out, and_9_out, and_10_out, and_11_out);
  or or_5 (Miss, and_12_out, and_13_out, and_14_out, and_15_out);
  or or_6 (Dirty, and_16_out, and_17_out);
  or or_7 (UpdateDirty, and_18_out, and_19_out);
  or or_8 (MemReadReq, and_20_out, and_21_out);
  or or_9 (ReadFromMemory, and_23_out, and_24_out);
  or or_10 (UpdateAge, and_25_out, and_26_out, and_27_out);
endmodule

module TestFSM (
  input  in_1,
  input  in_2,
  input  in_3,
  input  in_4,
  input  in_5
);

  wire Delay, Extraclkcycle, fsmout_1_dirty, fsmout_1_evict, fsmout_1_initialize, fsmout_1_memreadreq,
       fsmout_1_memwritereq, fsmout_1_miss, fsmout_1_readfrommemory, fsmout_1_ready, fsmout_1_updateage,
       fsmout_1_updatedc, fsmout_1_updatedirty, fsmout_1_updatetag, fsmout_1_updatevalid, fsmout_1_valid,
       multiplexer_2_out;
  wire [3:0] FSMNextState_nextstate, multiplexer_1_out, State, undriven;

  FSM FSMNextState (
    .StateIn(State), .DidContain(in_1), .Dirty(in_2), .Read(in_3), .Write(in_4),
    .NextState(FSMNextState_nextstate));
  Multiplexer #(.enable("false"), .width(4)) multiplexer_1 (
    .in0(4'b0000), .in1(undriven), .out(multiplexer_1_out), .sel(Extraclkcycle));
  Register #(.width(4)) register_1 (.D(FSMNextState_nextstate), .en(Delay), .clk(in_5), .Q(State));  // open: clr
  Register #(.width(1)) register_2 (.D(multiplexer_2_out), .clk(in_5), .Q(Delay));  // open: en, clr
  Multiplexer #(.enable("false")) multiplexer_2 (.in0(1'b1), .in1(1'b0), .out(multiplexer_2_out), .sel(Delay));
  Register #(.width(1)) register_3 (.D(1'b1), .clk(in_5), .Q(Extraclkcycle));  // open: en, clr
  // Probe on State
  // Probe on fsmout_1_initialize
  FSMOut fsmout_1 (
    .State(State), .Initialize(fsmout_1_initialize), .Ready(fsmout_1_ready), .Valid(fsmout_1_valid),
    .UpdateValid(fsmout_1_updatevalid), .UpdateTag(fsmout_1_updatetag), .Evict(fsmout_1_evict),
    .Miss(fsmout_1_miss), .Dirty(fsmout_1_dirty), .UpdateDirty(fsmout_1_updatedirty),
    .MemReadReq(fsmout_1_memreadreq), .MemWriteReq(fsmout_1_memwritereq),
    .ReadFromMemory(fsmout_1_readfrommemory), .UpdateAge(fsmout_1_updateage), .UpdateDC(fsmout_1_updatedc));
  // Probe on fsmout_1_ready
  // Probe on fsmout_1_valid
  // Probe on fsmout_1_updatevalid
  // Probe on fsmout_1_updatetag
  // Probe on fsmout_1_evict
  // Probe on fsmout_1_miss
  // Probe on fsmout_1_dirty
  // Probe on fsmout_1_updatedirty
  // Probe on fsmout_1_memreadreq
  // Probe on fsmout_1_memwritereq
  // Probe on fsmout_1_readfrommemory
  // Probe on fsmout_1_updateage
  // Probe on fsmout_1_updatedc

  // Other names for the same wires on the sheet: clk = in_5; DidContain = in_1; FeedFSMDirty = in_2; RCpuRead = in_3;
  //   RCpuWrite = in_4

  // Notes on the sheet:
  //   Relies on changing Did contain = 1 when getting new block
  //   Also relies on changin dirty and etc
endmodule
